// Logisim project 1.circ as structural Verilog: 2 circuits, main circuit main
module main (
  input  A,
  input  B,
  input  Vem_1,
  output S,
  output Vai_1
);

  wire and_1_out, and_2_out, not_1_out, or_1_out, xor_1_out;

  not not_1 (not_1_out, A);
  xor xor_1 (xor_1_out, A, B);
  or or_1 (or_1_out, B, Vem_1);
  and and_1 (and_1_out, or_1_out, not_1_out);
  and and_2 (and_2_out, B, Vem_1);
  xor xor_2 (S, xor_1_out, Vem_1);
  or or_2 (Vai_1, and_1_out, and_2_out);
endmodule

module _2 (
  input  in_1,
  input  in_2,
  input  in_3,
  output out_4,
  output out_5
);

  main main_1 (.A(in_1), .B(in_2), .Vem_1(in_3), .S(out_4), .Vai_1(out_5));
endmodule
