// Logisim project processador2v.circ as structural Verilog
module add_1bits (
  input  A,
  input  B,
  input  Vem_1,
  output S,
  output Vai_1
);

  wire and_1_out, and_2_out, or_1_out, xor_1_out;

  xor xor_1 (xor_1_out, A, B);
  or or_1 (or_1_out, B, Vem_1);
  and and_1 (and_1_out, B, Vem_1);
  xor xor_2 (S, xor_1_out, Vem_1);
  and and_2 (and_2_out, or_1_out, A);
  or or_2 (Vai_1, and_2_out, and_1_out);
endmodule

module sub_1bits (
  input  A,
  input  B,
  input  Vem_1,
  output S,
  output Vai_1
);

  wire and_1_out, and_2_out, not_1_out, or_1_out, xor_1_out;

  not not_1 (not_1_out, A);
  xor xor_1 (xor_1_out, A, B);
  or or_1 (or_1_out, B, Vem_1);
  and and_1 (and_1_out, B, Vem_1);
  xor xor_2 (S, xor_1_out, Vem_1);
  and and_2 (and_2_out, or_1_out, not_1_out);
  or or_2 (Vai_1, and_2_out, and_1_out);
endmodule

module somador_4bits (
  input  [3:0] B,
  input  [3:0] A,
  input  in_3,
  output out_4,
  output [3:0] out_5
);

  wire add_1bits_2_vai_1, add_1bits_3_vai_1, add_1bits_4_vai_1;

  add_1bits add_1bits_1 (.A(A[3]), .B(B[3]), .Vem_1(add_1bits_2_vai_1), .S(out_5[3]), .Vai_1(out_4));
  add_1bits add_1bits_2 (.A(A[2]), .B(B[2]), .Vem_1(add_1bits_3_vai_1), .S(out_5[2]), .Vai_1(add_1bits_2_vai_1));
  add_1bits add_1bits_3 (.A(A[1]), .B(B[1]), .Vem_1(add_1bits_4_vai_1), .S(out_5[1]), .Vai_1(add_1bits_3_vai_1));
  add_1bits add_1bits_4 (.A(A[0]), .B(B[0]), .Vem_1(in_3), .S(out_5[0]), .Vai_1(add_1bits_4_vai_1));
endmodule

module subtrator_4bits (
  input  [3:0] A,
  input  [3:0] B,
  input  Vem_1,
  output Vai_1,
  output [3:0] out_5
);

  wire sub_1bits_2_vai_1, sub_1bits_3_vai_1, sub_1bits_4_vai_1;

  sub_1bits sub_1bits_1 (.A(A[3]), .B(B[3]), .Vem_1(sub_1bits_2_vai_1), .S(out_5[3]), .Vai_1(Vai_1));
  sub_1bits sub_1bits_2 (.A(A[2]), .B(B[2]), .Vem_1(sub_1bits_3_vai_1), .S(out_5[2]), .Vai_1(sub_1bits_2_vai_1));
  sub_1bits sub_1bits_3 (.A(A[1]), .B(B[1]), .Vem_1(sub_1bits_4_vai_1), .S(out_5[1]), .Vai_1(sub_1bits_3_vai_1));
  sub_1bits sub_1bits_4 (.A(A[0]), .B(B[0]), .Vem_1(Vem_1), .S(out_5[0]), .Vai_1(sub_1bits_4_vai_1));
endmodule

module buffer (
  input  [3:0] B,
  input  in_2,
  output [3:0] S
);

  dec dec_1 ();  // open: in_1, s0, s1, s2, s3, s4, s5, s6, s7
  assign S[3] = in_2 ? B[3] : 1'bz;  // Controlled_Buffer controlled_buffer_1
  assign S[1] = in_2 ? B[1] : 1'bz;  // Controlled_Buffer controlled_buffer_2
  assign S[2] = in_2 ? B[2] : 1'bz;  // Controlled_Buffer controlled_buffer_3
  assign S[0] = in_2 ? B[0] : 1'bz;  // Controlled_Buffer controlled_buffer_4
endmodule

module buffer_inv (
  input  [3:0] B,
  input  in_2,
  output [3:0] S
);

  assign S[2] = in_2 ? ~B[2] : 1'bz;  // Controlled_Inverter controlled_inverter_1
  assign S[3] = in_2 ? ~B[3] : 1'bz;  // Controlled_Inverter controlled_inverter_2
  assign S[1] = in_2 ? ~B[1] : 1'bz;  // Controlled_Inverter controlled_inverter_3
  assign S[0] = in_2 ? ~B[0] : 1'bz;  // Controlled_Inverter controlled_inverter_4
endmodule

module dec (
  input  [2:0] in_1,
  output s0,
  output s1,
  output s2,
  output s3,
  output s4,
  output s5,
  output s6,
  output s7
);

  wire not_1_out, not_2_out, not_3_out, not_4_out, not_5_out, not_6_out, not_7_out, not_8_out, not_9_out,
       not_10_out, not_11_out, not_12_out;

  not not_1 (not_1_out, in_1[2]);
  and and_1 (s0, not_1_out, not_2_out, not_3_out);
  not not_2 (not_2_out, in_1[1]);
  not not_3 (not_3_out, in_1[0]);
  not not_4 (not_4_out, in_1[2]);
  not not_5 (not_5_out, in_1[1]);
  and and_2 (s1, not_4_out, not_5_out, in_1[0]);
  not not_6 (not_6_out, in_1[2]);
  and and_3 (s2, not_6_out, in_1[1], not_7_out);
  not not_7 (not_7_out, in_1[0]);
  not not_8 (not_8_out, in_1[2]);
  and and_4 (s3, not_8_out, in_1[1], in_1[0]);
  not not_9 (not_9_out, in_1[1]);
  and and_5 (s4, in_1[2], not_9_out, not_10_out);
  not not_10 (not_10_out, in_1[0]);
  and and_6 (s5, in_1[2], not_11_out, in_1[0]);
  not not_11 (not_11_out, in_1[1]);
  and and_7 (s6, in_1[2], in_1[1], not_12_out);
  not not_12 (not_12_out, in_1[0]);
  and and_8 (s7, in_1[2], in_1[1], in_1[0]);
endmodule

module rot_l (
  input  [3:0] ABCD,
  input  [1:0] XY,
  output [3:0] ABCD_2
);

  wire and_1_out, and_2_out, and_3_out, and_4_out, and_5_out, and_6_out, and_7_out, and_8_out, and_9_out;

  and and_1 (and_1_out, ~XY[1], ~XY[0], ABCD[3]);  // AND_Gate
  and and_2 (and_2_out, ~XY[1], XY[0], ABCD[2]);  // AND_Gate
  and and_3 (and_3_out, XY[1], ~XY[0], ABCD[1]);  // AND_Gate
  and and_4 (and_4_out, XY[1], XY[0], ABCD[0]);
  and and_5 (and_5_out, ~XY[1], ~XY[0], ABCD[2]);  // AND_Gate
  and and_6 (and_6_out, ~XY[1], XY[0], ABCD[1]);  // AND_Gate
  and and_7 (and_7_out, XY[1], ~XY[0], ABCD[0]);  // AND_Gate
  and and_8 (and_8_out, ~XY[1], ~XY[0], ABCD[1]);  // AND_Gate
  and and_9 (and_9_out, ~XY[1], XY[0], ABCD[0]);  // AND_Gate
  and and_10 (ABCD_2[0], ~XY[1], ~XY[0], ABCD[0]);  // AND_Gate
  or or_1 (ABCD_2[3], and_1_out, and_2_out, and_3_out, and_4_out);
  or or_2 (ABCD_2[2], and_5_out, and_6_out, and_7_out);
  or or_3 (ABCD_2[1], and_8_out, and_9_out);
endmodule

module rot_r (
  input  [3:0] ABCD,
  input  [1:0] XY,
  output [3:0] ABCD_2
);

  wire and_1_out, and_2_out, and_3_out, and_4_out, and_5_out, and_6_out, and_7_out, and_8_out, and_9_out;

  and and_1 (and_1_out, ~XY[1], ~XY[0], ABCD[0]);  // AND_Gate
  and and_2 (and_2_out, ~XY[1], XY[0], ABCD[1]);  // AND_Gate
  and and_3 (and_3_out, XY[1], ~XY[0], ABCD[2]);  // AND_Gate
  and and_4 (and_4_out, XY[1], XY[0], ABCD[3]);
  and and_5 (and_5_out, ~XY[1], ~XY[0], ABCD[1]);  // AND_Gate
  and and_6 (and_6_out, ~XY[1], XY[0], ABCD[2]);  // AND_Gate
  and and_7 (and_7_out, XY[1], ~XY[0], ABCD[3]);  // AND_Gate
  and and_8 (and_8_out, ~XY[1], ~XY[0], ABCD[2]);  // AND_Gate
  and and_9 (and_9_out, ~XY[1], XY[0], ABCD[3]);  // AND_Gate
  and and_10 (ABCD_2[3], ~XY[1], ~XY[0], ABCD[3]);  // AND_Gate
  or or_1 (ABCD_2[0], and_1_out, and_2_out, and_3_out, and_4_out);
  or or_2 (ABCD_2[1], and_5_out, and_6_out, and_7_out);
  or or_3 (ABCD_2[2], and_8_out, and_9_out);
endmodule

module or_4bits (
  input  [3:0] A,
  input  [3:0] B,
  output [3:0] S
);

  or or_1 (S[3], A[3], B[3]);
  or or_2 (S[2], A[2], B[2]);
  or or_3 (S[0], A[0], B[0]);
  or or_4 (S[1], A[1], B[1]);
endmodule

module ula (
  input  D,
  input  [3:0] A,
  input  [3:0] B,
  input  [2:0] Operacoes,
  output Overflow,
  output [3:0] Saida,
  output Zero
);

  wire and_1_out, and_2_out, dec_1_s0, dec_1_s1, dec_1_s2, dec_1_s3, dec_1_s4, dec_1_s5, dec_1_s6, dec_1_s7,
       not_1_out, somador_4bits_1_out_4, subtrator_4bits_1_vai_1;
  wire [3:0] buffer_5_s, or_4bits_1_s, rot_l_1_abcd_2, rot_r_1_abcd_2, somador_4bits_1_out_5,
       subtrator_4bits_1_out_5;

  or or_1 (Overflow, and_1_out, and_2_out);
  and and_1 (and_1_out, somador_4bits_1_out_4, dec_1_s1);
  and and_2 (and_2_out, subtrator_4bits_1_vai_1, dec_1_s2);
  dec dec_1 (
    .in_1(Operacoes), .s0(dec_1_s0), .s1(dec_1_s1), .s2(dec_1_s2), .s3(dec_1_s3), .s4(dec_1_s4),
    .s5(dec_1_s5), .s6(dec_1_s6), .s7(dec_1_s7));
  buffer buffer_1 (.in_2(dec_1_s0), .B(B), .S(Saida));
  nor nor_1 (Zero, dec_1_s7, dec_1_s6, Saida[0], Saida[1], Saida[2], Saida[3]);
  somador_4bits somador_4bits_1 (
    .B(B), .A(A), .out_4(somador_4bits_1_out_4), .out_5(somador_4bits_1_out_5), .in_3(1'b0));
  buffer buffer_2 (.in_2(dec_1_s1), .B(somador_4bits_1_out_5), .S(Saida));
  subtrator_4bits subtrator_4bits_1 (
    .B(B), .Vai_1(subtrator_4bits_1_vai_1), .out_5(subtrator_4bits_1_out_5), .Vem_1(1'b0), .A(A));
  buffer buffer_3 (.in_2(dec_1_s2), .B(subtrator_4bits_1_out_5), .S(Saida));
  buffer buffer_4 (.in_2(dec_1_s3), .B(or_4bits_1_s), .S(Saida));
  or_4bits or_4bits_1 (.A(A), .B(B), .S(or_4bits_1_s));
  buffer_inv buffer_inv_1 (.in_2(dec_1_s4), .B(B), .S(Saida));
  not not_1 (not_1_out, D);
  rot_r rot_r_1 (.ABCD(A), .XY(B[1:0]), .ABCD_2(rot_r_1_abcd_2));
  rot_l rot_l_1 (.ABCD(A), .XY(B[1:0]), .ABCD_2(rot_l_1_abcd_2));
  buffer buffer_5 (.in_2(D), .B(rot_r_1_abcd_2), .S(buffer_5_s));
  buffer buffer_6 (.in_2(not_1_out), .B(rot_l_1_abcd_2), .S(buffer_5_s));
  buffer buffer_7 (.in_2(dec_1_s5), .B(buffer_5_s), .S(Saida));
endmodule

module teste_ula (
  input  [3:0] A,
  input  [3:0] B,
  input  D,
  input  [2:0] Operacoes,
  output Overflow,
  output Zero,
  output [3:0] Saida
);

  // Probe on A
  ula ula_1 (.D(D), .A(A), .B(B), .Operacoes(Operacoes), .Overflow(Overflow), .Zero(Zero), .Saida(Saida));
  // Probe on Saida
  // Probe on B

  // Notes on the sheet:
  //   011 or
  //   001 soma
  //   010 sub
  //   100 inv b
  //   101 rotacionador
endmodule
